# Fritzing sketch simple (saved by Fritzing 0.8.5b)
breadboards: 2

parts:
  P1_LU = Pushbutton [package="[THT]"]
  P1_RU = Pushbutton [package="[THT]"]
  P1_LD = Pushbutton [package="[THT]"]
  P1_RD = Pushbutton [package="[THT]"]
  P1_CN = Pushbutton [package="[THT]"]
  P2_RU = Pushbutton [package="[THT]"]
  P2_LD = Pushbutton [package="[THT]"]
  P2_RD = Pushbutton [package="[THT]"]
  P2_CN = Pushbutton [package="[THT]"]
  TEST = Pushbutton [package="[THT]"]
  SERVICE = Pushbutton [package="[THT]"]
  R-P1-LU = Resistor [tolerance=±5% resistance=1k package=THT]
  R-P1-RU = Resistor [tolerance=±5% resistance=1k package=THT]
  R-P1-CN = Resistor [tolerance=±5% resistance=1k package=THT]
  R-P1-LD = Resistor [tolerance=±5% resistance=1k package=THT]
  R-P1-RD = Resistor [tolerance=±5% resistance=1k package=THT]
  R-TEST = Resistor [tolerance=±5% resistance=1k package=THT]
  R-SERVICE = Resistor [tolerance=±5% resistance=1k package=THT]
  R-P2-RU = Resistor [tolerance=±5% resistance=1k package=THT]
  R-P2-RD = Resistor [tolerance=±5% resistance=1k package=THT]
  R-P2-LU = Resistor [tolerance=±5% resistance=1k package=THT]
  R-P2-CN = Resistor [tolerance=±5% resistance=1k package=THT]
  P2_LU = Pushbutton [package="[THT]"]
  R-P2-LD = Resistor [tolerance=±5% resistance=1k package=THT]
  R-RESET = Resistor [tolerance=±5% resistance=1k package=THT]
  RESET = Pushbutton [package="[THT]"]
  XTAL1 = Crystal [frequency="16 Mhz" package=THT]
  C1 = Electrolytic Capacitor [capacitance=4.7µF package="100 mil [THT, electrolytic]"]
  CONN1 = USB connector [package=THT]
  D1 = Rectifier Diode [part_number=1N4001 package="300 mil [THT]"]
  D2 = Rectifier Diode [part_number=1N4001 package="300 mil [THT]"]
  R-USB-D+ = Resistor [tolerance=±5% resistance=68 package=THT]
  R-USB-D- = Resistor [tolerance=±5% resistance=68 package=THT]
  R-USB-PULLUP-D- = Resistor [tolerance=±5% resistance=1.5k package=THT]
  U1 = atmega328 [package=dip]

nets (from the schematic view):
  N1: P1_LU.Pin_1, P1_LU.Pin_2, R-P1-LU.Pin_1, U1.D8
  N2: P1_LU.Pin_3, P1_LU.Pin_4, P1_RU.Pin_3, P1_RU.Pin_4, P1_LD.Pin_3, P1_LD.Pin_4, P1_RD.Pin_3, P1_RD.Pin_4, P1_CN.Pin_3, P1_CN.Pin_4, P2_RU.Pin_1, P2_RU.Pin_2, P2_LD.Pin_1, P2_LD.Pin_2, P2_RD.Pin_1, P2_RD.Pin_2, P2_CN.Pin_1, P2_CN.Pin_2, TEST.Pin_3, TEST.Pin_4, SERVICE.Pin_1, SERVICE.Pin_2, P2_LU.Pin_1, P2_LU.Pin_2, RESET.Pin_3, RESET.Pin_4, C1.-, CONN1.chassis6, U1.GND
  N3: P1_RU.Pin_1, P1_RU.Pin_2, R-P1-RU.Pin_1, U1.D9_(PWM)
  N4: P1_LD.Pin_1, P1_LD.Pin_2, R-P1-LD.Pin_1, U1.D11_(PWM)
  N5: P1_RD.Pin_1, P1_RD.Pin_2, R-P1-RD.Pin_1, U1.D12
  N6: P1_CN.Pin_1, P1_CN.Pin_2, R-P1-CN.Pin_1, U1.D10_(PWM)
  N7: P2_RU.Pin_3, P2_RU.Pin_4, R-P2-RU.Pin_0, U1.A1
  N8: P2_LD.Pin_3, P2_LD.Pin_4, R-P2-LD.Pin_0, U1.A3
  N9: P2_RD.Pin_3, P2_RD.Pin_4, R-P2-RD.Pin_0, U1.A4
  N10: P2_CN.Pin_3, P2_CN.Pin_4, R-P2-CN.Pin_0, U1.A2
  N11: TEST.Pin_1, TEST.Pin_2, R-TEST.Pin_1, U1.D13
  N12: SERVICE.Pin_3, SERVICE.Pin_4, R-SERVICE.Pin_0, U1.A5
  N13: R-P1-LU.Pin_0, R-P1-RU.Pin_0, R-P1-CN.Pin_0, R-P1-LD.Pin_0, R-P1-RD.Pin_0, R-TEST.Pin_0, R-SERVICE.Pin_1, R-P2-RU.Pin_1, R-P2-RD.Pin_1, R-P2-LU.Pin_0, R-P2-CN.Pin_1, R-P2-LD.Pin_1, R-RESET.Pin_0, C1.+, D2.cathode, R-USB-PULLUP-D-.Pin_1, U1.VCC, U1.AVCC
  N14: R-P2-LU.Pin_1, P2_LU.Pin_3, P2_LU.Pin_4, U1.A0
  N15: R-RESET.Pin_1, RESET.Pin_1, RESET.Pin_2, U1.RESET
  N16: XTAL1.pin_0, U1.XLAT1
  N17: XTAL1.pin_1, U1.XLAT2
  N18: CONN1.5V, D1.anode
  N19: CONN1.d-, R-USB-D+.Pin_0
  N20: CONN1.d+, R-USB-D-.Pin_0, R-USB-PULLUP-D-.Pin_0
  N21: D1.cathode, D2.anode
  N22: R-USB-D+.Pin_1, U1.D1_(TX), U1.D2
  N23: R-USB-D-.Pin_1, U1.D0_(RX)
